// Logisim project Mano.circ as structural Verilog: 31 circuits, main circuit main
module main (
  input  RESET,
  output out_2
);

  wire \AC_Kontrolü_clear , \AC_Kontrolü_increment , \AC_Kontrolü_load , ALU_e_out, \AR_Kontrolü_clear ,
       \AR_Kontrolü_increment , \AR_Kontrolü_load , clear_t_1_t_count_clear, Clock, clock_1_out, Clr_T,
       \dr_kontrolü_1_increment , \dr_kontrolü_1_load , E, \E_Kontrolü_clear , \E_Kontrolü_comp ,
       \E_Kontrolü_load , FGI, \fgi_fgo_ien_kontrolü_1_fgo_j , \fgi_fgo_ien_kontrolü_1_fgo_k ,
       \fgi_fgo_ien_kontrolü_1_ien_j , \fgi_fgo_ien_kontrolü_1_ien_k , FGO, HLT, IEN, inp_kontrol_1_ld,
       \IR_Kontrolü_load , j_k_ff_1_q, not_1_out, not_2_out, not_3_out, or_1_out, or_2_out, or_3_out,
       or_4_out, or_5_out, or_6_out, \OUTR_Kontrolü_clear , \OUTR_Kontrolü_ld , \PC_Kontrolü_clear ,
       \PC_Kontrolü_increment , \PC_Kontrolü_load , R, \ram_kontrolü_1_load , \TR_Kontrolü_load ;
  wire [2:0] Select_bus_select, T;
  wire [6:0] INPUT;
  wire [7:0] INPR, OUTR;
  wire [11:0] AR, PC;
  wire [15:0] AC, ALU_bus_out, BUS_DATA, DR, IR, Memory_Data, ram_1_data, TR;

  Keyboard keyboard_1 (.clk(Clock), .re(inp_kontrol_1_ld), .clr(RESET), .data(INPUT));  // open: avail
  INP_Kontrol inp_kontrol_1 (.T(T), .IR(IR), .LD(inp_kontrol_1_ld));
  \E_Kontrolü  \E_Kontrolü  (
    .T(T), .IR(IR), .Comp(\E_Kontrolü_comp ), .Clear(\E_Kontrolü_clear ), .Load(\E_Kontrolü_load ));
  E u_E (
    .E_IN(ALU_e_out), .Comp(\E_Kontrolü_comp ), .load(\E_Kontrolü_load ), .Clock(Clock), .Clear(or_1_out),
    .E_OUT(out_2));
  or or_1 (or_1_out, \E_Kontrolü_clear , RESET);
  \RAM_Kontrolü  \ram_kontrolü_1  (.T(T), .R(R), .IR(IR), .Load(\ram_kontrolü_1_load ));
  \PC_Kontrolü  \PC_Kontrolü  (
    .T(T), .FGI(FGI), .FGO(FGO), .E(E), .R(R), .IR(IR), .DR(DR), .AC(AC), .Load(\PC_Kontrolü_load ),
    .Increment(\PC_Kontrolü_increment ), .Clear(\PC_Kontrolü_clear ));
  ALU ALU (.DR(DR), .AC(AC), .INPR(INPR), .BUS_OUT(ALU_bus_out), .E_OUT(ALU_e_out), .T(T), .IR(IR));  // open: E_In
  \OUTR_Kontrolü  \OUTR_Kontrolü  (.T(T), .IR(IR), .LD(\OUTR_Kontrolü_ld ), .Clear(\OUTR_Kontrolü_clear ));
  RAM #(.addrWidth(12), .dataWidth(16)) ram_1 (
    .addr(AR), .data(ram_1_data), .clk(Clock), .ld(\ram_kontrolü_1_load ));  // open: sel, clr
  \AR_Kontrolü  \AR_Kontrolü  (
    .T(T), .R(R), .IR(IR), .Load(\AR_Kontrolü_load ), .Clear(\AR_Kontrolü_clear ),
    .Increment(\AR_Kontrolü_increment ));
  or or_2 (or_2_out, \PC_Kontrolü_clear , RESET);
  \DR_Kontrolü  \dr_kontrolü_1  (.T(T), .IR(IR), .Load(\dr_kontrolü_1_load ), .Increment(\dr_kontrolü_1_increment ));
  or or_3 (or_3_out, \AC_Kontrolü_clear , RESET);
  \AC_Kontrolü  \AC_Kontrolü  (
    .T(T), .IR(IR), .Clear(\AC_Kontrolü_clear ), .Increment(\AC_Kontrolü_increment ),
    .LOAD(\AC_Kontrolü_load ));
  \IR_Kontrolü  \IR_Kontrolü  (.T(T), .R(R), .Load(\IR_Kontrolü_load ));
  \TR_Kontrolü  \TR_Kontrolü  (.T(T), .R(R), .Load(\TR_Kontrolü_load ));
  or or_4 (or_4_out, \OUTR_Kontrolü_clear , RESET);
  assign ram_1_data = not_1_out ? BUS_DATA : 16'bz;  // Controlled_Buffer controlled_buffer_1
  assign Memory_Data = \ram_kontrolü_1_load  ? ram_1_data : 16'bz;  // Controlled_Buffer controlled_buffer_2
  not not_1 (not_1_out, \ram_kontrolü_1_load );
  _12_bit_Register u_AR (
    .Clear(or_5_out), .Load(\AR_Kontrolü_load ), .Clk(Clock), .Increment(\AR_Kontrolü_increment ),
    .Register_OUT(AR), .Register_IN(BUS_DATA[11:0]));
  or or_5 (or_5_out, \AR_Kontrolü_clear , RESET);
  _12_bit_Register u_PC (
    .Clear(or_2_out), .Load(\PC_Kontrolü_load ), .Clk(Clock), .Increment(\PC_Kontrolü_increment ),
    .Register_OUT(PC), .Register_IN(BUS_DATA[11:0]));
  _16_bit_Register u_DR (
    .Clear(RESET), .Load(\dr_kontrolü_1_load ), .Increment(\dr_kontrolü_1_increment ), .Register_OUT(DR),
    .Register_IN(BUS_DATA), .Clk(Clock));
  _16_bit_Register u_AC (
    .Clear(or_3_out), .Load(\AC_Kontrolü_load ), .Increment(\AC_Kontrolü_increment ), .Register_OUT(AC),
    .Register_IN(ALU_bus_out), .Clk(Clock));
  IR u_IR (
    .Clear(RESET), .Load(\IR_Kontrolü_load ), .Clk(Clock), .Increment(1'b0), .Register_OUT(IR),
    .Register_IN(BUS_DATA), .HLT(HLT));
  _16_bit_Register u_TR (
    .Clear(RESET), .Load(\TR_Kontrolü_load ), .Increment(1'b0), .Register_OUT(TR), .Register_IN(BUS_DATA),
    .Clk(Clock));
  _8_bit_register u_OUTR (
    .Clear(or_4_out), .Load(\OUTR_Kontrolü_ld ), .Clk(Clock), .Increment(1'b0), .Register_OUT(OUTR),
    .Register_IN(BUS_DATA[7:0]));
  Bus_Select Select (.T(T), .R(R), .IR(IR), .Bus_Select(Select_bus_select));
  Clear_T clear_t_1 (.T(T), .R(R), .IR(IR), .T_count_clear(clear_t_1_t_count_clear));
  TTY tty_1 (.data(OUTR[6:0]), .clk(Clock), .clr(RESET));  // open: we
  or or_6 (or_6_out, Clr_T, RESET);
  IEN ien_1 (.IEN_J(\fgi_fgo_ien_kontrolü_1_ien_j ), .IEN_K(\fgi_fgo_ien_kontrolü_1_ien_k ), .Clock(Clock), .IEN(IEN));
  _4_bit_counter u_4_bit_counter_1 (.Clk(Clock), .Bit_0(T[0]), .Bit_1(T[1]), .Bit_2(T[2]), .Clear(or_6_out));
  Multiplexer #(.select(3), .width(16), .enable("false")) multiplexer_1 (
    .in1({4'b0000, AR}), .in2({4'b0000, PC}), .in3(DR), .in4(AC), .in5(IR), .in6(TR), .in7(Memory_Data),
    .out(BUS_DATA), .sel(Select_bus_select));  // open: in0
  or or_7 (Clr_T, clear_t_1_t_count_clear, HLT);
  FGO fgo_1 (.FGO_J(\fgi_fgo_ien_kontrolü_1_fgo_j ), .FGO_K(\fgi_fgo_ien_kontrolü_1_fgo_k ), .Clock(Clock), .FGO(FGO));
  \FGI_FGO_IEN_Kontrolü  \fgi_fgo_ien_kontrolü_1  (
    .T(T), .IR(IR), .INPR(INPR), .R(R), .FGO_K(\fgi_fgo_ien_kontrolü_1_fgo_k ),
    .IEN_K(\fgi_fgo_ien_kontrolü_1_ien_k ), .IEN_J(\fgi_fgo_ien_kontrolü_1_ien_j ),
    .FGO_J(\fgi_fgo_ien_kontrolü_1_fgo_j ), .FGI(FGI), .Reset(RESET), .Clock(Clock));
  Hex_Digit_Display hex_digit_display_1 (.value(BUS_DATA[15:12]));  // open: dp
  Hex_Digit_Display hex_digit_display_2 (.value(OUTR[7:4]));  // open: dp
  Hex_Digit_Display hex_digit_display_3 (.value(INPR[7:4]));  // open: dp
  Hex_Digit_Display hex_digit_display_4 (.value(BUS_DATA[7:4]));  // open: dp
  Hex_Digit_Display hex_digit_display_5 (.value(BUS_DATA[11:8]));  // open: dp
  Hex_Digit_Display hex_digit_display_6 (.value(OUTR[3:0]));  // open: dp
  Hex_Digit_Display hex_digit_display_7 (.value(INPR[3:0]));  // open: dp
  \R_Kontrolü  \r_kontrolü_1  (.T(T), .IEN(IEN), .FGO(FGO), .FGI(FGI), .R(R));
  Hex_Digit_Display hex_digit_display_8 (.value(BUS_DATA[3:0]));  // open: dp
  Hex_Digit_Display hex_digit_display_9 (.value({1'b0, T}));  // open: dp
  Hex_Digit_Display hex_digit_display_10 (.value(AR[11:8]));  // open: dp
  Hex_Digit_Display hex_digit_display_11 (.value(PC[11:8]));  // open: dp
  Hex_Digit_Display hex_digit_display_12 (.value(DR[15:12]));  // open: dp
  Hex_Digit_Display hex_digit_display_13 (.value(AC[15:12]));  // open: dp
  Hex_Digit_Display hex_digit_display_14 (.value(IR[15:12]));  // open: dp
  Hex_Digit_Display hex_digit_display_15 (.value(TR[15:12]));  // open: dp
  _8_bit_register u_8_bit_register_1 (
    .Clear(RESET), .Load(not_2_out), .Clk(Clock), .Increment(1'b0), .Register_OUT(INPR),
    .Register_IN({1'b0, INPUT}));
  not not_2 (not_2_out, FGI);
  Hex_Digit_Display hex_digit_display_16 (.value(AR[7:4]));  // open: dp
  Hex_Digit_Display hex_digit_display_17 (.value(PC[7:4]));  // open: dp
  Hex_Digit_Display hex_digit_display_18 (.value(DR[11:8]));  // open: dp
  Hex_Digit_Display hex_digit_display_19 (.value(AC[11:8]));  // open: dp
  Hex_Digit_Display hex_digit_display_20 (.value(IR[11:8]));  // open: dp
  Hex_Digit_Display hex_digit_display_21 (.value(TR[11:8]));  // open: dp
  and and_1 (Clock, clock_1_out, not_3_out);
  Hex_Digit_Display hex_digit_display_22 (.value(AR[3:0]));  // open: dp
  Hex_Digit_Display hex_digit_display_23 (.value(PC[3:0]));  // open: dp
  Hex_Digit_Display hex_digit_display_24 (.value(DR[7:4]));  // open: dp
  Hex_Digit_Display hex_digit_display_25 (.value(AC[7:4]));  // open: dp
  Hex_Digit_Display hex_digit_display_26 (.value(IR[7:4]));  // open: dp
  Hex_Digit_Display hex_digit_display_27 (.value(IR[3:0]));  // open: dp
  Hex_Digit_Display hex_digit_display_28 (.value(TR[3:0]));  // open: dp
  Hex_Digit_Display hex_digit_display_29 (.value(TR[7:4]));  // open: dp
  not not_3 (not_3_out, j_k_ff_1_q);
  Hex_Digit_Display hex_digit_display_30 (.value(DR[3:0]));  // open: dp
  Hex_Digit_Display hex_digit_display_31 (.value(AC[3:0]));  // open: dp
  Clock clock_1 (.out(clock_1_out));
  J_K_Flip_Flop j_k_ff_1 (.J(HLT), .clk(clock_1_out), .K(RESET), .Q(j_k_ff_1_q));  // open: Qn, preset, en, reset

  // Notes on the sheet:
  //   OUTR
  //   INPR
  //   T
  //   AR
  //   PC
  //   DR
  //   AC
  //   IR
  //   TR
endmodule

module _16_bit_Register (
  input  Clear,
  input  Load,
  input  Clk,
  input  Increment,
  input  [15:0] Register_IN,
  output [15:0] Register_OUT
);

  wire and_1_out, and_2_out, and_3_out, and_4_out, and_5_out, and_6_out, and_7_out, and_8_out, and_9_out,
       and_10_out, and_11_out, and_12_out, and_13_out, and_14_out, and_15_out, and_16_out, and_17_out,
       and_18_out, and_19_out, and_20_out, and_21_out, and_22_out, and_23_out, and_24_out, and_25_out,
       and_26_out, and_27_out, and_28_out, and_29_out, and_30_out, and_31_out, and_32_out, and_33_out,
       and_34_out, and_35_out, and_36_out, and_37_out, and_38_out, and_39_out, and_40_out, and_41_out,
       and_42_out, and_43_out, and_44_out, and_45_out, and_46_out, and_47_out, and_48_out, and_49_out,
       not_1_out, not_2_out, not_3_out, not_4_out, not_5_out, not_6_out, not_7_out, not_8_out, not_9_out,
       not_10_out, not_11_out, not_12_out, not_13_out, not_14_out, not_15_out, not_16_out, not_17_out,
       not_18_out, or_1_out, or_2_out, or_3_out, or_4_out, or_5_out, or_6_out, or_7_out, or_8_out, or_9_out,
       or_10_out, or_11_out, or_12_out, or_13_out, or_14_out, or_15_out, or_16_out, or_17_out, or_18_out,
       or_19_out, or_20_out, or_21_out, or_22_out, or_23_out, or_24_out, or_25_out, or_26_out, or_27_out,
       or_28_out, or_29_out, or_30_out, or_31_out, or_32_out;

  not not_1 (not_1_out, Clear);
  not not_2 (not_2_out, Load);
  and and_1 (and_1_out, not_1_out, Load);
  and and_2 (and_2_out, not_1_out, not_2_out, Increment);
  not not_3 (not_3_out, Register_IN[0]);
  not not_4 (not_4_out, Register_IN[1]);
  not not_5 (not_5_out, Register_IN[2]);
  not not_6 (not_6_out, Register_IN[3]);
  not not_7 (not_7_out, Register_IN[4]);
  not not_8 (not_8_out, Register_IN[5]);
  not not_9 (not_9_out, Register_IN[6]);
  not not_10 (not_10_out, Register_IN[7]);
  not not_11 (not_11_out, Register_IN[8]);
  not not_12 (not_12_out, Register_IN[9]);
  not not_13 (not_13_out, Register_IN[10]);
  not not_14 (not_14_out, Register_IN[11]);
  not not_15 (not_15_out, Register_IN[12]);
  not not_16 (not_16_out, Register_IN[13]);
  not not_17 (not_17_out, Register_IN[14]);
  not not_18 (not_18_out, Register_IN[15]);
  and and_3 (and_3_out, and_1_out, Register_IN[0]);
  and and_4 (and_4_out, and_1_out, not_3_out);
  and and_5 (and_5_out, and_2_out, Register_OUT[0]);
  and and_6 (and_6_out, and_1_out, Register_IN[1]);
  and and_7 (and_7_out, and_1_out, not_4_out);
  and and_8 (and_8_out, and_5_out, Register_OUT[1]);
  and and_9 (and_9_out, and_1_out, Register_IN[2]);
  and and_10 (and_10_out, and_1_out, not_5_out);
  and and_11 (and_11_out, and_8_out, Register_OUT[2]);
  and and_12 (and_12_out, and_1_out, Register_IN[3]);
  and and_13 (and_13_out, and_1_out, not_6_out);
  and and_14 (and_14_out, and_1_out, Register_IN[4]);
  and and_15 (and_15_out, and_1_out, not_7_out);
  and and_16 (and_16_out, and_1_out, Register_IN[5]);
  and and_17 (and_17_out, and_1_out, not_8_out);
  and and_18 (and_18_out, and_1_out, Register_IN[6]);
  and and_19 (and_19_out, and_1_out, not_9_out);
  and and_20 (and_20_out, and_1_out, Register_IN[7]);
  and and_21 (and_21_out, and_1_out, not_10_out);
  and and_22 (and_22_out, and_1_out, Register_IN[8]);
  and and_23 (and_23_out, and_1_out, not_11_out);
  and and_24 (and_24_out, and_1_out, Register_IN[9]);
  and and_25 (and_25_out, and_1_out, not_12_out);
  and and_26 (and_26_out, and_1_out, Register_IN[10]);
  and and_27 (and_27_out, and_1_out, not_13_out);
  and and_28 (and_28_out, and_1_out, Register_IN[11]);
  and and_29 (and_29_out, and_1_out, not_14_out);
  and and_30 (and_30_out, and_1_out, Register_IN[12]);
  and and_31 (and_31_out, and_1_out, not_15_out);
  and and_32 (and_32_out, and_1_out, Register_IN[13]);
  and and_33 (and_33_out, and_1_out, not_16_out);
  and and_34 (and_34_out, and_1_out, Register_IN[14]);
  and and_35 (and_35_out, and_1_out, not_17_out);
  and and_36 (and_36_out, and_1_out, Register_IN[15]);
  and and_37 (and_37_out, and_1_out, not_18_out);
  or or_1 (or_1_out, and_2_out, and_3_out);
  or or_2 (or_2_out, Clear, and_2_out, and_4_out);
  or or_3 (or_3_out, and_5_out, and_6_out);
  or or_4 (or_4_out, Clear, and_5_out, and_7_out);
  or or_5 (or_5_out, and_8_out, and_9_out);
  or or_6 (or_6_out, Clear, and_8_out, and_10_out);
  or or_7 (or_7_out, and_11_out, and_12_out);
  or or_8 (or_8_out, Clear, and_11_out, and_13_out);
  and and_38 (and_38_out, and_11_out, Register_OUT[3]);
  or or_9 (or_9_out, and_38_out, and_14_out);
  or or_10 (or_10_out, Clear, and_38_out, and_15_out);
  and and_39 (and_39_out, and_38_out, Register_OUT[4]);
  or or_11 (or_11_out, and_39_out, and_16_out);
  or or_12 (or_12_out, Clear, and_39_out, and_17_out);
  and and_40 (and_40_out, and_39_out, Register_OUT[5]);
  or or_13 (or_13_out, and_40_out, and_18_out);
  or or_14 (or_14_out, Clear, and_40_out, and_19_out);
  and and_41 (and_41_out, and_40_out, Register_OUT[6]);
  or or_15 (or_15_out, and_41_out, and_20_out);
  or or_16 (or_16_out, Clear, and_41_out, and_21_out);
  and and_42 (and_42_out, and_41_out, Register_OUT[7]);
  or or_17 (or_17_out, and_42_out, and_22_out);
  or or_18 (or_18_out, Clear, and_42_out, and_23_out);
  and and_43 (and_43_out, and_42_out, Register_OUT[8]);
  or or_19 (or_19_out, and_43_out, and_24_out);
  or or_20 (or_20_out, Clear, and_43_out, and_25_out);
  and and_44 (and_44_out, and_43_out, Register_OUT[9]);
  or or_21 (or_21_out, and_44_out, and_26_out);
  or or_22 (or_22_out, Clear, and_44_out, and_27_out);
  and and_45 (and_45_out, and_44_out, Register_OUT[10]);
  or or_23 (or_23_out, and_45_out, and_28_out);
  or or_24 (or_24_out, Clear, and_45_out, and_29_out);
  and and_46 (and_46_out, and_45_out, Register_OUT[11]);
  or or_25 (or_25_out, and_46_out, and_30_out);
  or or_26 (or_26_out, Clear, and_46_out, and_31_out);
  and and_47 (and_47_out, and_46_out, Register_OUT[12]);
  or or_27 (or_27_out, and_47_out, and_32_out);
  or or_28 (or_28_out, Clear, and_47_out, and_33_out);
  and and_48 (and_48_out, and_47_out, Register_OUT[13]);
  or or_29 (or_29_out, and_48_out, and_34_out);
  or or_30 (or_30_out, Clear, and_48_out, and_35_out);
  and and_49 (and_49_out, and_48_out, Register_OUT[14]);
  or or_31 (or_31_out, and_49_out, and_36_out);
  or or_32 (or_32_out, Clear, and_49_out, and_37_out);
  J_K_Flip_Flop j_k_ff_1 (.J(or_1_out), .clk(Clk), .K(or_2_out), .Q(Register_OUT[0]));  // open: Qn, preset, en, reset
  J_K_Flip_Flop j_k_ff_2 (.J(or_3_out), .clk(Clk), .K(or_4_out), .Q(Register_OUT[1]));  // open: Qn, preset, en, reset
  J_K_Flip_Flop j_k_ff_3 (.J(or_5_out), .clk(Clk), .K(or_6_out), .Q(Register_OUT[2]));  // open: Qn, preset, en, reset
  J_K_Flip_Flop j_k_ff_4 (.J(or_7_out), .clk(Clk), .K(or_8_out), .Q(Register_OUT[3]));  // open: Qn, preset, en, reset
  J_K_Flip_Flop j_k_ff_5 (.J(or_9_out), .clk(Clk), .K(or_10_out), .Q(Register_OUT[4]));  // open: Qn, preset, en, reset
  J_K_Flip_Flop j_k_ff_6 (.J(or_11_out), .clk(Clk), .K(or_12_out), .Q(Register_OUT[5]));  // open: Qn, preset, en, reset
  J_K_Flip_Flop j_k_ff_7 (.J(or_13_out), .clk(Clk), .K(or_14_out), .Q(Register_OUT[6]));  // open: Qn, preset, en, reset
  J_K_Flip_Flop j_k_ff_8 (.J(or_15_out), .clk(Clk), .K(or_16_out), .Q(Register_OUT[7]));  // open: Qn, preset, en, reset
  J_K_Flip_Flop j_k_ff_9 (.J(or_17_out), .clk(Clk), .K(or_18_out), .Q(Register_OUT[8]));  // open: Qn, preset, en, reset
  J_K_Flip_Flop j_k_ff_10 (
    .J(or_19_out), .clk(Clk), .K(or_20_out), .Q(Register_OUT[9]));  // open: Qn, preset, en, reset
  J_K_Flip_Flop j_k_ff_11 (
    .J(or_21_out), .clk(Clk), .K(or_22_out), .Q(Register_OUT[10]));  // open: Qn, preset, en, reset
  J_K_Flip_Flop j_k_ff_12 (
    .J(or_23_out), .clk(Clk), .K(or_24_out), .Q(Register_OUT[11]));  // open: Qn, preset, en, reset
  J_K_Flip_Flop j_k_ff_13 (
    .J(or_25_out), .clk(Clk), .K(or_26_out), .Q(Register_OUT[12]));  // open: Qn, preset, en, reset
  J_K_Flip_Flop j_k_ff_14 (
    .J(or_27_out), .clk(Clk), .K(or_28_out), .Q(Register_OUT[13]));  // open: Qn, preset, en, reset
  J_K_Flip_Flop j_k_ff_15 (
    .J(or_29_out), .clk(Clk), .K(or_30_out), .Q(Register_OUT[14]));  // open: Qn, preset, en, reset
  J_K_Flip_Flop j_k_ff_16 (
    .J(or_31_out), .clk(Clk), .K(or_32_out), .Q(Register_OUT[15]));  // open: Qn, preset, en, reset
  // AND_Gate and_50 has open pins: in0=Register_OUT[15], in1=and_49_out, out=open

  // Other names for the same wires on the sheet: r0 = Register_IN[0]; r1 = Register_IN[1]; r2 = Register_IN[2];
  //   r3 = Register_IN[3]; r4 = Register_IN[4]; r5 = Register_IN[5]; r6 = Register_IN[6]; r7 = Register_IN[7];
  //   r8 = Register_IN[8]; r9 = Register_IN[9]; r10 = Register_IN[10]; r11 = Register_IN[11]; r12 = Register_IN[12];
  //   r13 = Register_IN[13]; r14 = Register_IN[14]; r15 = Register_IN[15]; d0 = Register_OUT[0]; d1 = Register_OUT[1];
  //   d2 = Register_OUT[2]; d3 = Register_OUT[3]; d4 = Register_OUT[4]; d5 = Register_OUT[5]; d6 = Register_OUT[6];
  //   d7 = Register_OUT[7]; d8 = Register_OUT[8]; d9 = Register_OUT[9]; d10 = Register_OUT[10];
  //   d11 = Register_OUT[11]; d12 = Register_OUT[12]; d13 = Register_OUT[13]; d14 = Register_OUT[14];
  //   d15 = Register_OUT[15]
endmodule

module _12_bit_Register (
  input  Clear,
  input  Load,
  input  Clk,
  input  Increment,
  input  [11:0] Register_IN,
  output [11:0] Register_OUT
);

  wire and_1_out, and_2_out, and_3_out, and_4_out, and_5_out, and_6_out, and_7_out, and_8_out, and_9_out,
       and_10_out, and_11_out, and_12_out, and_13_out, and_14_out, and_15_out, and_16_out, and_17_out,
       and_18_out, and_19_out, and_20_out, and_21_out, and_22_out, and_23_out, and_24_out, and_25_out,
       and_26_out, and_27_out, and_28_out, and_29_out, and_30_out, and_31_out, and_32_out, and_33_out,
       and_34_out, and_35_out, and_36_out, and_37_out, not_1_out, not_2_out, not_3_out, not_4_out, not_5_out,
       not_6_out, not_7_out, not_8_out, not_9_out, not_10_out, not_11_out, not_12_out, not_13_out,
       not_14_out, or_1_out, or_2_out, or_3_out, or_4_out, or_5_out, or_6_out, or_7_out, or_8_out, or_9_out,
       or_10_out, or_11_out, or_12_out, or_13_out, or_14_out, or_15_out, or_16_out, or_17_out, or_18_out,
       or_19_out, or_20_out, or_21_out, or_22_out, or_23_out, or_24_out;

  not not_1 (not_1_out, Clear);
  not not_2 (not_2_out, Load);
  and and_1 (and_1_out, not_1_out, Load);
  and and_2 (and_2_out, not_1_out, not_2_out, Increment);
  not not_3 (not_3_out, Register_IN[0]);
  not not_4 (not_4_out, Register_IN[1]);
  not not_5 (not_5_out, Register_IN[2]);
  not not_6 (not_6_out, Register_IN[3]);
  not not_7 (not_7_out, Register_IN[4]);
  not not_8 (not_8_out, Register_IN[5]);
  not not_9 (not_9_out, Register_IN[6]);
  not not_10 (not_10_out, Register_IN[7]);
  not not_11 (not_11_out, Register_IN[8]);
  not not_12 (not_12_out, Register_IN[9]);
  not not_13 (not_13_out, Register_IN[10]);
  not not_14 (not_14_out, Register_IN[11]);
  and and_3 (and_3_out, and_1_out, Register_IN[0]);
  and and_4 (and_4_out, and_1_out, not_3_out);
  and and_5 (and_5_out, and_2_out, Register_OUT[0]);
  and and_6 (and_6_out, and_1_out, Register_IN[1]);
  and and_7 (and_7_out, and_1_out, not_4_out);
  and and_8 (and_8_out, and_5_out, Register_OUT[1]);
  and and_9 (and_9_out, and_1_out, Register_IN[2]);
  and and_10 (and_10_out, and_1_out, not_5_out);
  and and_11 (and_11_out, and_8_out, Register_OUT[2]);
  and and_12 (and_12_out, and_1_out, Register_IN[3]);
  and and_13 (and_13_out, and_1_out, not_6_out);
  and and_14 (and_14_out, and_1_out, Register_IN[4]);
  and and_15 (and_15_out, and_1_out, not_7_out);
  and and_16 (and_16_out, and_1_out, Register_IN[5]);
  and and_17 (and_17_out, and_1_out, not_8_out);
  and and_18 (and_18_out, and_1_out, Register_IN[6]);
  and and_19 (and_19_out, and_1_out, not_9_out);
  and and_20 (and_20_out, and_1_out, Register_IN[7]);
  and and_21 (and_21_out, and_1_out, not_10_out);
  and and_22 (and_22_out, and_1_out, Register_IN[8]);
  and and_23 (and_23_out, and_1_out, not_11_out);
  and and_24 (and_24_out, and_1_out, Register_IN[9]);
  and and_25 (and_25_out, and_1_out, not_12_out);
  and and_26 (and_26_out, and_1_out, Register_IN[10]);
  and and_27 (and_27_out, and_1_out, not_13_out);
  and and_28 (and_28_out, and_1_out, Register_IN[11]);
  and and_29 (and_29_out, and_1_out, not_14_out);
  or or_1 (or_1_out, and_2_out, and_3_out);
  or or_2 (or_2_out, Clear, and_2_out, and_4_out);
  or or_3 (or_3_out, and_5_out, and_6_out);
  or or_4 (or_4_out, Clear, and_5_out, and_7_out);
  or or_5 (or_5_out, and_8_out, and_9_out);
  or or_6 (or_6_out, Clear, and_8_out, and_10_out);
  or or_7 (or_7_out, and_11_out, and_12_out);
  or or_8 (or_8_out, Clear, and_11_out, and_13_out);
  and and_30 (and_30_out, and_11_out, Register_OUT[3]);
  or or_9 (or_9_out, and_30_out, and_14_out);
  or or_10 (or_10_out, Clear, and_30_out, and_15_out);
  and and_31 (and_31_out, and_30_out, Register_OUT[4]);
  or or_11 (or_11_out, and_31_out, and_16_out);
  or or_12 (or_12_out, Clear, and_31_out, and_17_out);
  and and_32 (and_32_out, and_31_out, Register_OUT[5]);
  or or_13 (or_13_out, and_32_out, and_18_out);
  or or_14 (or_14_out, Clear, and_32_out, and_19_out);
  and and_33 (and_33_out, and_32_out, Register_OUT[6]);
  or or_15 (or_15_out, and_33_out, and_20_out);
  or or_16 (or_16_out, Clear, and_33_out, and_21_out);
  and and_34 (and_34_out, and_33_out, Register_OUT[7]);
  or or_17 (or_17_out, and_34_out, and_22_out);
  or or_18 (or_18_out, Clear, and_34_out, and_23_out);
  and and_35 (and_35_out, and_34_out, Register_OUT[8]);
  or or_19 (or_19_out, and_35_out, and_24_out);
  or or_20 (or_20_out, Clear, and_35_out, and_25_out);
  and and_36 (and_36_out, and_35_out, Register_OUT[9]);
  or or_21 (or_21_out, and_36_out, and_26_out);
  or or_22 (or_22_out, Clear, and_36_out, and_27_out);
  and and_37 (and_37_out, and_36_out, Register_OUT[10]);
  or or_23 (or_23_out, and_37_out, and_28_out);
  or or_24 (or_24_out, Clear, and_37_out, and_29_out);
  // AND_Gate and_38 has open pins: in0=and_37_out, in1=Register_OUT[11], out=open
  J_K_Flip_Flop j_k_ff_1 (.J(or_1_out), .clk(Clk), .K(or_2_out), .Q(Register_OUT[0]));  // open: Qn, preset, en, reset
  J_K_Flip_Flop j_k_ff_2 (.J(or_3_out), .clk(Clk), .K(or_4_out), .Q(Register_OUT[1]));  // open: Qn, preset, en, reset
  J_K_Flip_Flop j_k_ff_3 (.J(or_5_out), .clk(Clk), .K(or_6_out), .Q(Register_OUT[2]));  // open: Qn, preset, en, reset
  J_K_Flip_Flop j_k_ff_4 (.J(or_7_out), .clk(Clk), .K(or_8_out), .Q(Register_OUT[3]));  // open: Qn, preset, en, reset
  J_K_Flip_Flop j_k_ff_5 (.J(or_9_out), .clk(Clk), .K(or_10_out), .Q(Register_OUT[4]));  // open: Qn, preset, en, reset
  J_K_Flip_Flop j_k_ff_6 (.J(or_11_out), .clk(Clk), .K(or_12_out), .Q(Register_OUT[5]));  // open: Qn, preset, en, reset
  J_K_Flip_Flop j_k_ff_7 (.J(or_13_out), .clk(Clk), .K(or_14_out), .Q(Register_OUT[6]));  // open: Qn, preset, en, reset
  J_K_Flip_Flop j_k_ff_8 (.J(or_15_out), .clk(Clk), .K(or_16_out), .Q(Register_OUT[7]));  // open: Qn, preset, en, reset
  J_K_Flip_Flop j_k_ff_9 (.J(or_17_out), .clk(Clk), .K(or_18_out), .Q(Register_OUT[8]));  // open: Qn, preset, en, reset
  J_K_Flip_Flop j_k_ff_10 (
    .J(or_19_out), .clk(Clk), .K(or_20_out), .Q(Register_OUT[9]));  // open: Qn, preset, en, reset
  J_K_Flip_Flop j_k_ff_11 (
    .J(or_21_out), .clk(Clk), .K(or_22_out), .Q(Register_OUT[10]));  // open: Qn, preset, en, reset
  J_K_Flip_Flop j_k_ff_12 (
    .J(or_23_out), .clk(Clk), .K(or_24_out), .Q(Register_OUT[11]));  // open: Qn, preset, en, reset

  // Other names for the same wires on the sheet: r0 = Register_IN[0]; r1 = Register_IN[1]; r2 = Register_IN[2];
  //   r3 = Register_IN[3]; r4 = Register_IN[4]; r5 = Register_IN[5]; r6 = Register_IN[6]; r7 = Register_IN[7];
  //   r8 = Register_IN[8]; r9 = Register_IN[9]; r10 = Register_IN[10]; r11 = Register_IN[11]; d0 = Register_OUT[0];
  //   d1 = Register_OUT[1]; d2 = Register_OUT[2]; d3 = Register_OUT[3]; d4 = Register_OUT[4]; d5 = Register_OUT[5];
  //   d6 = Register_OUT[6]; d7 = Register_OUT[7]; d8 = Register_OUT[8]; d9 = Register_OUT[9]; d10 = Register_OUT[10];
  //   d11 = Register_OUT[11]
endmodule

module _8_bit_register (
  input  Clear,
  input  Load,
  input  Clk,
  input  Increment,
  input  [7:0] Register_IN,
  output [7:0] Register_OUT
);

  wire and_1_out, and_2_out, and_3_out, and_4_out, and_5_out, and_6_out, and_7_out, and_8_out, and_9_out,
       and_10_out, and_11_out, and_12_out, and_13_out, and_14_out, and_15_out, and_16_out, and_17_out,
       and_18_out, and_19_out, and_20_out, and_21_out, and_22_out, and_23_out, and_24_out, and_25_out,
       not_1_out, not_2_out, not_3_out, not_4_out, not_5_out, not_6_out, not_7_out, not_8_out, not_9_out,
       not_10_out, or_1_out, or_2_out, or_3_out, or_4_out, or_5_out, or_6_out, or_7_out, or_8_out, or_9_out,
       or_10_out, or_11_out, or_12_out, or_13_out, or_14_out, or_15_out, or_16_out;

  not not_1 (not_1_out, Clear);
  not not_2 (not_2_out, Load);
  and and_1 (and_1_out, not_1_out, Load);
  and and_2 (and_2_out, not_1_out, not_2_out, Increment);
  not not_3 (not_3_out, Register_IN[0]);
  not not_4 (not_4_out, Register_IN[1]);
  not not_5 (not_5_out, Register_IN[2]);
  not not_6 (not_6_out, Register_IN[3]);
  not not_7 (not_7_out, Register_IN[4]);
  not not_8 (not_8_out, Register_IN[5]);
  not not_9 (not_9_out, Register_IN[6]);
  not not_10 (not_10_out, Register_IN[7]);
  and and_3 (and_3_out, and_1_out, Register_IN[0]);
  and and_4 (and_4_out, and_1_out, not_3_out);
  and and_5 (and_5_out, and_2_out, Register_OUT[0]);
  and and_6 (and_6_out, and_1_out, Register_IN[1]);
  and and_7 (and_7_out, and_1_out, not_4_out);
  and and_8 (and_8_out, and_5_out, Register_OUT[1]);
  and and_9 (and_9_out, and_1_out, Register_IN[2]);
  and and_10 (and_10_out, and_1_out, not_5_out);
  and and_11 (and_11_out, and_8_out, Register_OUT[2]);
  and and_12 (and_12_out, and_1_out, Register_IN[3]);
  and and_13 (and_13_out, and_1_out, not_6_out);
  and and_14 (and_14_out, and_1_out, Register_IN[4]);
  and and_15 (and_15_out, and_1_out, not_7_out);
  and and_16 (and_16_out, and_1_out, Register_IN[5]);
  and and_17 (and_17_out, and_1_out, not_8_out);
  and and_18 (and_18_out, and_1_out, Register_IN[6]);
  and and_19 (and_19_out, and_1_out, not_9_out);
  and and_20 (and_20_out, and_1_out, Register_IN[7]);
  and and_21 (and_21_out, and_1_out, not_10_out);
  or or_1 (or_1_out, and_2_out, and_3_out);
  or or_2 (or_2_out, Clear, and_2_out, and_4_out);
  or or_3 (or_3_out, and_5_out, and_6_out);
  or or_4 (or_4_out, Clear, and_5_out, and_7_out);
  or or_5 (or_5_out, and_8_out, and_9_out);
  or or_6 (or_6_out, Clear, and_8_out, and_10_out);
  or or_7 (or_7_out, and_11_out, and_12_out);
  or or_8 (or_8_out, Clear, and_11_out, and_13_out);
  and and_22 (and_22_out, and_11_out, Register_OUT[3]);
  or or_9 (or_9_out, and_22_out, and_14_out);
  or or_10 (or_10_out, Clear, and_22_out, and_15_out);
  and and_23 (and_23_out, and_22_out, Register_OUT[4]);
  or or_11 (or_11_out, and_23_out, and_16_out);
  or or_12 (or_12_out, Clear, and_23_out, and_17_out);
  and and_24 (and_24_out, and_23_out, Register_OUT[5]);
  or or_13 (or_13_out, and_24_out, and_18_out);
  or or_14 (or_14_out, Clear, and_24_out, and_19_out);
  and and_25 (and_25_out, and_24_out, Register_OUT[6]);
  or or_15 (or_15_out, and_25_out, and_20_out);
  or or_16 (or_16_out, Clear, and_25_out, and_21_out);
  // AND_Gate and_26 has open pins: in0=and_25_out, in1=Register_OUT[7], out=open
  J_K_Flip_Flop j_k_ff_1 (.J(or_1_out), .clk(Clk), .K(or_2_out), .Q(Register_OUT[0]));  // open: Qn, preset, en, reset
  J_K_Flip_Flop j_k_ff_2 (.J(or_3_out), .clk(Clk), .K(or_4_out), .Q(Register_OUT[1]));  // open: Qn, preset, en, reset
  J_K_Flip_Flop j_k_ff_3 (.J(or_5_out), .clk(Clk), .K(or_6_out), .Q(Register_OUT[2]));  // open: Qn, preset, en, reset
  J_K_Flip_Flop j_k_ff_4 (.J(or_7_out), .clk(Clk), .K(or_8_out), .Q(Register_OUT[3]));  // open: Qn, preset, en, reset
  J_K_Flip_Flop j_k_ff_5 (.J(or_9_out), .clk(Clk), .K(or_10_out), .Q(Register_OUT[4]));  // open: Qn, preset, en, reset
  J_K_Flip_Flop j_k_ff_6 (.J(or_11_out), .clk(Clk), .K(or_12_out), .Q(Register_OUT[5]));  // open: Qn, preset, en, reset
  J_K_Flip_Flop j_k_ff_7 (.J(or_13_out), .clk(Clk), .K(or_14_out), .Q(Register_OUT[6]));  // open: Qn, preset, en, reset
  J_K_Flip_Flop j_k_ff_8 (.J(or_15_out), .clk(Clk), .K(or_16_out), .Q(Register_OUT[7]));  // open: Qn, preset, en, reset

  // Other names for the same wires on the sheet: r0 = Register_IN[0]; r1 = Register_IN[1]; r2 = Register_IN[2];
  //   r3 = Register_IN[3]; r4 = Register_IN[4]; r5 = Register_IN[5]; r6 = Register_IN[6]; r7 = Register_IN[7];
  //   d0 = Register_OUT[0]; d1 = Register_OUT[1]; d2 = Register_OUT[2]; d3 = Register_OUT[3]; d4 = Register_OUT[4];
  //   d5 = Register_OUT[5]; d6 = Register_OUT[6]; d7 = Register_OUT[7]
endmodule

module ALU (
  input  [2:0] T,
  input  [15:0] IR,
  input  E_In,
  input  [15:0] DR,
  input  [15:0] AC,
  input  [7:0] INPR,
  output [15:0] BUS_OUT,
  output E_OUT
);

  wire \alu_i_ç_1_cout , and_1_out, and_4_out, and_5_out, and_6_out, and_7_out, and_8_out, and_9_out,
       and_10_out, decoder_1_out0, decoder_1_out1, decoder_1_out2, decoder_1_out3, decoder_1_out4,
       decoder_1_out5, decoder_1_out6, decoder_1_out7, decoder_2_out0, decoder_2_out1, decoder_2_out2,
       decoder_2_out3, decoder_2_out4, decoder_2_out5, decoder_2_out6, decoder_2_out7, not_1_out, or_1_out,
       p, r;
  wire [4:0] Select;

  \ALU_İÇ  \alu_i̇ç_1  (
    .Cin(E_In), .Select(Select), .DR(DR), .AC(AC), .INPR(INPR), .BUS_OUT(BUS_OUT), .Cout(\alu_i_ç_1_cout ));
  and and_1 (and_1_out, ~Select[4], ~Select[3], ~Select[2], ~Select[1], Select[0]);  // AND_Gate
  assign E_OUT = and_1_out ? \alu_i_ç_1_cout  : 1'bz;  // Controlled_Buffer controlled_buffer_1
  Decoder #(.select(3), .enable("false")) decoder_1 (
    .out0(decoder_1_out0), .out1(decoder_1_out1), .out2(decoder_1_out2), .out3(decoder_1_out3),
    .out4(decoder_1_out4), .out5(decoder_1_out5), .out6(decoder_1_out6), .out7(decoder_1_out7), .sel(T));
  Decoder #(.select(3), .enable("false")) decoder_2 (
    .out0(decoder_2_out0), .out1(decoder_2_out1), .out2(decoder_2_out2), .out3(decoder_2_out3),
    .out4(decoder_2_out4), .out5(decoder_2_out5), .out6(decoder_2_out6), .out7(decoder_2_out7),
    .sel(IR[14:12]));
  and and_2 (r, decoder_2_out7, ~IR[15], decoder_1_out3);  // AND_Gate
  and and_3 (p, decoder_2_out7, IR[15], decoder_1_out3);
  and and_4 (and_4_out, decoder_2_out0, decoder_1_out5);
  and and_5 (and_5_out, decoder_2_out1, decoder_1_out5);
  and and_6 (and_6_out, decoder_2_out2, decoder_1_out5);
  and and_7 (and_7_out, IR[9], r);
  and and_8 (and_8_out, IR[7], r);
  and and_9 (and_9_out, IR[6], r);
  and and_10 (and_10_out, IR[11], p);
  or or_1 (or_1_out, and_6_out, and_7_out, and_9_out, and_8_out, and_4_out, and_5_out, and_10_out);
  not not_1 (not_1_out, or_1_out);
  Priority_Encoder #(.select(5)) priority_encoder_1 (
    .in0(and_6_out), .in1(and_5_out), .in4(and_4_out), .in7(and_7_out), .in8(and_8_out), .in12(and_9_out),
    .in16(and_10_out), .in20(not_1_out), .out(Select));  // open: in2, in3, in5, in6, in9, in10, in11, in13, in14, in15, in17, in18, in19, in21, in22, in23, in24, in25, in26, in27, in28, in29, in30, in31, gs, en_out, en_in
endmodule

module _4_bit_counter (
  input  Clk,
  input  Clear,
  output Bit_0,
  output Bit_1,
  output Bit_2
);

  wire d_ff_1_qn, d_ff_2_qn, d_ff_3_qn;

  D_Flip_Flop d_ff_1 (.clk(Clk), .D(d_ff_1_qn), .Q(Bit_0), .Qn(d_ff_1_qn), .reset(Clear));  // open: preset, en
  D_Flip_Flop d_ff_2 (.clk(d_ff_1_qn), .D(d_ff_2_qn), .Q(Bit_1), .Qn(d_ff_2_qn), .reset(Clear));  // open: preset, en
  D_Flip_Flop d_ff_3 (.clk(d_ff_2_qn), .D(d_ff_3_qn), .Q(Bit_2), .Qn(d_ff_3_qn), .reset(Clear));  // open: preset, en
endmodule

module Aritmetik_Birim (
  input  [1:0] Select,
  input  Cin,
  input  [15:0] DR,
  input  [15:0] AC,
  output [15:0] \Çıkış ,
  output Cout
);

  wire adder_1_cout, adder_2_cout, adder_3_cout, adder_4_cout, adder_5_cout, adder_6_cout, adder_7_cout,
       adder_8_cout, adder_9_cout, adder_10_cout, adder_11_cout, adder_12_cout, adder_13_cout, adder_14_cout,
       adder_15_cout, multiplexer_1_out, multiplexer_2_out, multiplexer_3_out, multiplexer_4_out,
       multiplexer_5_out, multiplexer_6_out, multiplexer_7_out, multiplexer_8_out, multiplexer_9_out,
       multiplexer_10_out, multiplexer_11_out, multiplexer_12_out, multiplexer_13_out, multiplexer_14_out,
       multiplexer_15_out, multiplexer_16_out, not_1_out, not_2_out, not_3_out, not_4_out, not_5_out,
       not_6_out, not_7_out, not_8_out, not_9_out, not_10_out, not_11_out, not_12_out, not_13_out,
       not_14_out, not_15_out, not_16_out, not_17_out;

  not not_1 (not_1_out, AC[0]);
  not not_2 (not_2_out, 1'b0);
  not not_3 (not_3_out, AC[1]);
  not not_4 (not_4_out, AC[2]);
  not not_5 (not_5_out, AC[3]);
  not not_6 (not_6_out, AC[4]);
  not not_7 (not_7_out, AC[5]);
  not not_8 (not_8_out, AC[6]);
  not not_9 (not_9_out, AC[7]);
  not not_10 (not_10_out, AC[8]);
  not not_11 (not_11_out, AC[9]);
  not not_12 (not_12_out, AC[10]);
  not not_13 (not_13_out, AC[13]);
  not not_14 (not_14_out, AC[14]);
  not not_15 (not_15_out, AC[15]);
  not not_16 (not_16_out, AC[11]);
  not not_17 (not_17_out, AC[12]);
  Multiplexer #(.select(2), .enable("false")) multiplexer_1 (
    .in0(1'b0), .in1(AC[0]), .in2(not_1_out), .in3(not_2_out), .out(multiplexer_1_out), .sel(Select));
  Multiplexer #(.select(2), .enable("false")) multiplexer_2 (
    .in0(1'b0), .in1(AC[1]), .in2(not_3_out), .in3(not_2_out), .out(multiplexer_2_out), .sel(Select));
  Multiplexer #(.select(2), .enable("false")) multiplexer_3 (
    .in0(1'b0), .in1(AC[2]), .in2(not_4_out), .in3(not_2_out), .out(multiplexer_3_out), .sel(Select));
  Multiplexer #(.select(2), .enable("false")) multiplexer_4 (
    .in0(1'b0), .in1(AC[3]), .in2(not_5_out), .in3(not_2_out), .out(multiplexer_4_out), .sel(Select));
  Multiplexer #(.select(2), .enable("false")) multiplexer_5 (
    .in0(1'b0), .in1(AC[4]), .in2(not_6_out), .in3(not_2_out), .out(multiplexer_5_out), .sel(Select));
  Multiplexer #(.select(2), .enable("false")) multiplexer_6 (
    .in0(1'b0), .in1(AC[5]), .in2(not_7_out), .in3(not_2_out), .out(multiplexer_6_out), .sel(Select));
  Multiplexer #(.select(2), .enable("false")) multiplexer_7 (
    .in0(1'b0), .in1(AC[6]), .in2(not_8_out), .in3(not_2_out), .out(multiplexer_7_out), .sel(Select));
  Multiplexer #(.select(2), .enable("false")) multiplexer_8 (
    .in0(1'b0), .in1(AC[7]), .in2(not_9_out), .in3(not_2_out), .out(multiplexer_8_out), .sel(Select));
  Multiplexer #(.select(2), .enable("false")) multiplexer_9 (
    .in0(1'b0), .in1(AC[8]), .in2(not_10_out), .in3(not_2_out), .out(multiplexer_9_out), .sel(Select));
  Multiplexer #(.select(2), .enable("false")) multiplexer_10 (
    .in0(1'b0), .in1(AC[9]), .in2(not_11_out), .in3(not_2_out), .out(multiplexer_10_out), .sel(Select));
  Multiplexer #(.select(2), .enable("false")) multiplexer_11 (
    .in0(1'b0), .in1(AC[10]), .in2(not_12_out), .in3(not_2_out), .out(multiplexer_11_out), .sel(Select));
  Multiplexer #(.select(2), .enable("false")) multiplexer_12 (
    .in0(1'b0), .in1(AC[11]), .in2(not_16_out), .in3(not_2_out), .out(multiplexer_12_out), .sel(Select));
  Multiplexer #(.select(2), .enable("false")) multiplexer_13 (
    .in0(1'b0), .in1(AC[12]), .in2(not_17_out), .in3(not_2_out), .out(multiplexer_13_out), .sel(Select));
  Multiplexer #(.select(2), .enable("false")) multiplexer_14 (
    .in0(1'b0), .in1(AC[13]), .in2(not_13_out), .in3(not_2_out), .out(multiplexer_14_out), .sel(Select));
  Multiplexer #(.select(2), .enable("false")) multiplexer_15 (
    .in0(1'b0), .in1(AC[14]), .in2(not_14_out), .in3(not_2_out), .out(multiplexer_15_out), .sel(Select));
  Multiplexer #(.select(2), .enable("false")) multiplexer_16 (
    .in0(1'b0), .in1(AC[15]), .in2(not_15_out), .in3(not_2_out), .out(multiplexer_16_out), .sel(Select));
  Adder #(.width(1)) adder_1 (.a(DR[0]), .b(multiplexer_1_out), .out(\Çıkış [0]), .cin(Cin), .cout(adder_1_cout));
  Adder #(.width(1)) adder_2 (
    .a(DR[1]), .b(multiplexer_2_out), .out(\Çıkış [1]), .cin(adder_1_cout), .cout(adder_2_cout));
  Adder #(.width(1)) adder_3 (
    .a(DR[2]), .b(multiplexer_3_out), .out(\Çıkış [2]), .cin(adder_2_cout), .cout(adder_3_cout));
  Adder #(.width(1)) adder_4 (
    .a(DR[3]), .b(multiplexer_4_out), .out(\Çıkış [3]), .cin(adder_3_cout), .cout(adder_4_cout));
  Adder #(.width(1)) adder_5 (
    .a(DR[4]), .b(multiplexer_5_out), .out(\Çıkış [4]), .cin(adder_4_cout), .cout(adder_5_cout));
  Adder #(.width(1)) adder_6 (
    .a(DR[5]), .b(multiplexer_6_out), .out(\Çıkış [5]), .cin(adder_5_cout), .cout(adder_6_cout));
  Adder #(.width(1)) adder_7 (
    .a(DR[6]), .b(multiplexer_7_out), .out(\Çıkış [6]), .cin(adder_6_cout), .cout(adder_7_cout));
  Adder #(.width(1)) adder_8 (
    .a(DR[7]), .b(multiplexer_8_out), .out(\Çıkış [7]), .cin(adder_7_cout), .cout(adder_8_cout));
  Adder #(.width(1)) adder_9 (
    .a(DR[8]), .b(multiplexer_9_out), .out(\Çıkış [8]), .cin(adder_8_cout), .cout(adder_9_cout));
  Adder #(.width(1)) adder_10 (
    .a(DR[9]), .b(multiplexer_10_out), .out(\Çıkış [9]), .cin(adder_9_cout), .cout(adder_10_cout));
  Adder #(.width(1)) adder_11 (
    .a(DR[10]), .b(multiplexer_11_out), .out(\Çıkış [10]), .cin(adder_10_cout), .cout(adder_11_cout));
  Adder #(.width(1)) adder_12 (
    .a(DR[11]), .b(multiplexer_12_out), .out(\Çıkış [11]), .cin(adder_11_cout), .cout(adder_12_cout));
  Adder #(.width(1)) adder_13 (
    .a(DR[12]), .b(multiplexer_13_out), .out(\Çıkış [12]), .cin(adder_12_cout), .cout(adder_13_cout));
  Adder #(.width(1)) adder_14 (
    .a(DR[13]), .b(multiplexer_14_out), .out(\Çıkış [13]), .cin(adder_13_cout), .cout(adder_14_cout));
  Adder #(.width(1)) adder_15 (
    .a(DR[14]), .b(multiplexer_15_out), .out(\Çıkış [14]), .cin(adder_14_cout), .cout(adder_15_cout));
  Adder #(.width(1)) adder_16 (.a(DR[15]), .b(multiplexer_16_out), .out(\Çıkış [15]), .cin(adder_15_cout), .cout(Cout));
endmodule

module \Mantık_Birimi  (
  input  [1:0] Select,
  input  [15:0] DR,
  input  [15:0] AC,
  output [15:0] out_4
);

  wire [15:0] and_1_out, not_1_out, or_1_out, xor_1_out;

  assign and_1_out = DR & AC;  // AND_Gate and_1, 16 bits wide
  assign or_1_out = DR | AC;  // OR_Gate or_1, 16 bits wide
  assign xor_1_out = DR ^ AC;  // XOR_Gate xor_1, 16 bits wide
  assign not_1_out = ~AC;  // NOT_Gate not_1, 16 bits wide
  Multiplexer #(.select(2), .width(16), .enable("false")) multiplexer_1 (
    .in0(and_1_out), .in1(or_1_out), .in2(xor_1_out), .in3(not_1_out), .out(out_4), .sel(Select));
endmodule

module \Kaydırma_Birimi  (
  input  Select,
  input  [15:0] A,
  output [15:0] \Çıkış 
);

  Multiplexer #(.enable("false")) multiplexer_1 (.in0(A[1]), .in1(A[15]), .out(\Çıkış [0]), .sel(Select));
  Multiplexer #(.enable("false")) multiplexer_2 (.in0(A[2]), .in1(A[0]), .out(\Çıkış [1]), .sel(Select));
  Multiplexer #(.enable("false")) multiplexer_3 (.in0(A[3]), .in1(A[1]), .out(\Çıkış [2]), .sel(Select));
  Multiplexer #(.enable("false")) multiplexer_4 (.in0(A[4]), .in1(A[2]), .out(\Çıkış [3]), .sel(Select));
  Multiplexer #(.enable("false")) multiplexer_5 (.in0(A[5]), .in1(A[3]), .out(\Çıkış [4]), .sel(Select));
  Multiplexer #(.enable("false")) multiplexer_6 (.in0(A[6]), .in1(A[4]), .out(\Çıkış [5]), .sel(Select));
  Multiplexer #(.enable("false")) multiplexer_7 (.in0(A[7]), .in1(A[5]), .out(\Çıkış [6]), .sel(Select));
  Multiplexer #(.enable("false")) multiplexer_8 (.in0(A[8]), .in1(A[6]), .out(\Çıkış [7]), .sel(Select));
  Multiplexer #(.enable("false")) multiplexer_9 (.in0(A[9]), .in1(A[7]), .out(\Çıkış [8]), .sel(Select));
  Multiplexer #(.enable("false")) multiplexer_10 (.in0(A[10]), .in1(A[8]), .out(\Çıkış [9]), .sel(Select));
  Multiplexer #(.enable("false")) multiplexer_11 (.in0(A[11]), .in1(A[9]), .out(\Çıkış [10]), .sel(Select));
  Multiplexer #(.enable("false")) multiplexer_12 (.in0(A[12]), .in1(A[10]), .out(\Çıkış [11]), .sel(Select));
  Multiplexer #(.enable("false")) multiplexer_13 (.in0(A[13]), .in1(A[11]), .out(\Çıkış [12]), .sel(Select));
  Multiplexer #(.enable("false")) multiplexer_14 (.in0(A[14]), .in1(A[12]), .out(\Çıkış [13]), .sel(Select));
  Multiplexer #(.enable("false")) multiplexer_15 (.in0(A[15]), .in1(A[13]), .out(\Çıkış [14]), .sel(Select));
  Multiplexer #(.enable("false")) multiplexer_16 (.in0(A[0]), .in1(A[14]), .out(\Çıkış [15]), .sel(Select));

  // Other names for the same wires on the sheet: E = A[0]; E1 = A[15]
endmodule

module \ALU_İÇ  (
  input  Cin,
  input  [4:0] Select,
  input  [15:0] DR,
  input  [15:0] AC,
  input  [7:0] INPR,
  output [15:0] BUS_OUT,
  output Cout
);

  wire [15:0] \aritmetik_birim_1_çıkış , \kaydırma_birimi_1_çıkış , \mantık_birimi_1_out_4 ;

  Aritmetik_Birim aritmetik_birim_1 (
    .DR(DR), .AC(AC), .Select(Select[1:0]), .Cin(Cin), .\Çıkış (\aritmetik_birim_1_çıkış ), .Cout(Cout));
  \Mantık_Birimi  \mantık_birimi_1  (.Select(Select[1:0]), .DR(DR), .AC(AC), .out_4(\mantık_birimi_1_out_4 ));
  \Kaydırma_Birimi  \kaydırma_birimi_1  (.A(AC), .Select(Select[2]), .\Çıkış (\kaydırma_birimi_1_çıkış ));
  Multiplexer #(.select(3), .width(16), .enable("false")) multiplexer_1 (
    .in0(\aritmetik_birim_1_çıkış ), .in1(\mantık_birimi_1_out_4 ), .in2(\kaydırma_birimi_1_çıkış ),
    .in3(\kaydırma_birimi_1_çıkış ), .in4({{8{1'b0}}, INPR}), .in5(AC), .in7(DR), .out(BUS_OUT),
    .sel(Select[4:2]));  // open: in6
endmodule

module FGI (
  input  FGI_J,
  input  FGI_K,
  input  Clock,
  output FGI
);

  J_K_Flip_Flop j_k_ff_1 (.J(FGI_J), .clk(Clock), .K(FGI_K), .Q(FGI));  // open: Qn, preset, en, reset
endmodule

module FGO (
  input  FGO_J,
  input  FGO_K,
  input  Clock,
  output FGO
);

  J_K_Flip_Flop j_k_ff_1 (.J(FGO_J), .clk(Clock), .K(FGO_K), .Q(FGO));  // open: Qn, preset, en, reset
endmodule

module \FGI_FGO_IEN_Kontrolü  (
  input  [2:0] T,
  input  [15:0] IR,
  input  [7:0] INPR,
  input  R,
  input  Clock,
  input  Reset,
  output FGO_K,
  output FGI,
  output IEN_K,
  output IEN_J,
  output FGO_J
);

  wire and_2_out, and_3_out, and_4_out, and_7_out, decoder_1_out1, decoder_1_out2, decoder_1_out3,
       decoder_1_out4, decoder_1_out5, decoder_1_out6, decoder_1_out7, decoder_2_out0, decoder_2_out1,
       decoder_2_out2, decoder_2_out3, decoder_2_out4, decoder_2_out5, decoder_2_out6, decoder_2_out7,
       or_1_out, or_2_out, p;

  Decoder #(.select(3), .enable("false")) decoder_1 (
    .out0(FGO_J), .out1(decoder_1_out1), .out2(decoder_1_out2), .out3(decoder_1_out3), .out4(decoder_1_out4),
    .out5(decoder_1_out5), .out6(decoder_1_out6), .out7(decoder_1_out7), .sel(T));
  Decoder #(.select(3), .enable("false")) decoder_2 (
    .out0(decoder_2_out0), .out1(decoder_2_out1), .out2(decoder_2_out2), .out3(decoder_2_out3),
    .out4(decoder_2_out4), .out5(decoder_2_out5), .out6(decoder_2_out6), .out7(decoder_2_out7),
    .sel(IR[14:12]));
  and and_1 (p, decoder_2_out7, IR[15], decoder_1_out3);
  and and_2 (and_2_out, p, IR[11]);
  and and_3 (and_3_out, decoder_1_out2, R);
  and and_4 (and_4_out, IR[6], p);
  and and_5 (IEN_J, p, IR[7]);
  and and_6 (FGO_K, p, IR[10]);
  or or_1 (or_1_out, INPR[0], INPR[1], INPR[2], INPR[3], INPR[4], INPR[5], INPR[6], INPR[7]);
  or or_2 (or_2_out, and_2_out, Reset, and_7_out);
  or or_3 (IEN_K, and_3_out, and_4_out);
  and and_7 (and_7_out, p, IR[10]);
  J_K_Flip_Flop j_k_ff_1 (.J(or_1_out), .clk(Clock), .K(or_2_out), .Q(FGI));  // open: Qn, preset, en, reset

  // Other names for the same wires on the sheet: B6 = IR[6]; B7 = IR[7]; B10 = IR[10]; B11 = IR[11]
endmodule

module IEN (
  input  IEN_J,
  input  IEN_K,
  input  Clock,
  output IEN
);

  J_K_Flip_Flop j_k_ff_1 (.J(IEN_J), .clk(Clock), .K(IEN_K), .Q(IEN));  // open: Qn, preset, en, reset
endmodule

// R Kontrol
module \R_Kontrolü  (
  input  [2:0] T,
  input  IEN,
  input  FGO,
  input  FGI,
  output R
);

  wire and_1_out, and_2_out, and_3_out, decoder_1_out0, decoder_1_out1, decoder_1_out2, or_1_out;

  Decoder #(.select(3), .enable("false")) decoder_1 (
    .out0(decoder_1_out0), .out1(decoder_1_out1), .out2(decoder_1_out2), .sel(T));  // open: out3, out4, out5, out6, out7
  or or_1 (or_1_out, FGO, FGI);
  and and_1 (and_1_out, ~decoder_1_out0, ~decoder_1_out1, ~decoder_1_out2);  // AND_Gate
  and and_2 (and_2_out, IEN, and_1_out, or_1_out);
  and and_3 (and_3_out, decoder_1_out2, R);
  J_K_Flip_Flop j_k_ff_1 (.J(and_2_out), .clk(T[0]), .K(and_3_out), .Q(R));  // open: Qn, preset, en, reset
endmodule

module Bus_Select (
  input  [15:0] IR,
  input  [2:0] T,
  input  R,
  output [2:0] Bus_Select
);

  wire and_2_out, and_3_out, and_4_out, and_5_out, and_6_out, and_7_out, and_8_out, and_9_out, and_10_out,
       and_11_out, and_12_out, and_13_out, and_14_out, decoder_1_out0, decoder_1_out1, decoder_1_out2,
       decoder_1_out3, decoder_1_out4, decoder_1_out5, decoder_1_out6, decoder_1_out7, decoder_2_out0,
       decoder_2_out1, decoder_2_out2, decoder_2_out3, decoder_2_out4, decoder_2_out5, decoder_2_out6,
       decoder_2_out7, or_1_out, or_2_out, or_3_out, or_4_out, or_5_out, or_6_out, p;
  wire [2:0] priority_encoder_1_out;

  Decoder #(.select(3), .enable("false")) decoder_1 (
    .out0(decoder_1_out0), .out1(decoder_1_out1), .out2(decoder_1_out2), .out3(decoder_1_out3),
    .out4(decoder_1_out4), .out5(decoder_1_out5), .out6(decoder_1_out6), .out7(decoder_1_out7), .sel(T));
  Decoder #(.select(3), .enable("false")) decoder_2 (
    .out0(decoder_2_out0), .out1(decoder_2_out1), .out2(decoder_2_out2), .out3(decoder_2_out3),
    .out4(decoder_2_out4), .out5(decoder_2_out5), .out6(decoder_2_out6), .out7(decoder_2_out7),
    .sel(IR[14:12]));
  and and_1 (p, decoder_2_out7, IR[15], decoder_1_out3);
  and and_2 (and_2_out, decoder_2_out5, decoder_1_out4);
  and and_3 (and_3_out, decoder_1_out4, decoder_2_out4);
  and and_4 (and_4_out, decoder_2_out5, decoder_1_out5);
  and and_5 (and_5_out, decoder_2_out6, decoder_1_out6);
  and and_6 (and_6_out, decoder_2_out2, decoder_1_out5);
  and and_7 (and_7_out, decoder_2_out3, decoder_1_out4);
  and and_8 (and_8_out, IR[10], p);
  and and_9 (and_9_out, decoder_1_out2, ~R);  // AND_Gate
  and and_10 (and_10_out, decoder_1_out1, R);
  and and_11 (and_11_out, decoder_1_out1, ~R);  // AND_Gate
  and and_12 (and_12_out, ~decoder_2_out7, IR[15], decoder_1_out3);  // AND_Gate
  or or_1 (or_1_out, decoder_2_out0, decoder_2_out1, decoder_2_out2, decoder_2_out6);
  and and_13 (and_13_out, or_1_out, decoder_1_out4);
  or or_2 (or_2_out, decoder_1_out0, and_2_out);
  or or_3 (or_3_out, and_3_out, and_4_out);
  or or_4 (or_4_out, and_5_out, and_6_out);
  or or_5 (or_5_out, and_7_out, and_8_out);
  or or_6 (or_6_out, and_11_out, and_12_out, and_13_out);
  and and_14 (and_14_out, ~or_3_out, ~or_2_out, ~or_4_out, ~or_5_out, ~and_9_out, ~and_10_out, ~or_6_out);  // AND_Gate
  Priority_Encoder priority_encoder_1 (
    .in0(and_14_out), .in1(or_3_out), .in2(or_2_out), .in3(or_4_out), .in4(or_5_out), .in5(and_9_out),
    .in6(and_10_out), .in7(or_6_out), .out(priority_encoder_1_out));  // open: en_in, gs, en_out
  Multiplexer #(.select(3), .width(3), .enable("false")) multiplexer_1 (
    .in0(3'b000), .in1(3'b001), .in2(3'b010), .in3(3'b011), .in4(3'b100), .in5(3'b101), .in6(3'b110),
    .in7(3'b111), .out(Bus_Select), .sel(priority_encoder_1_out));
endmodule

module Clear_T (
  input  [15:0] IR,
  input  [2:0] T,
  input  R,
  output T_count_clear
);

  wire and_1_out, and_2_out, and_3_out, and_4_out, and_5_out, and_6_out, and_7_out, decoder_1_out0,
       decoder_1_out1, decoder_1_out2, decoder_1_out3, decoder_1_out4, decoder_1_out5, decoder_1_out6,
       decoder_1_out7, decoder_2_out0, decoder_2_out1, decoder_2_out2, decoder_2_out3, decoder_2_out4,
       decoder_2_out5, decoder_2_out6, decoder_2_out7, or_1_out;

  Decoder #(.select(3), .enable("false")) decoder_1 (
    .out0(decoder_1_out0), .out1(decoder_1_out1), .out2(decoder_1_out2), .out3(decoder_1_out3),
    .out4(decoder_1_out4), .out5(decoder_1_out5), .out6(decoder_1_out6), .out7(decoder_1_out7), .sel(T));
  Decoder #(.select(3), .enable("false")) decoder_2 (
    .out0(decoder_2_out0), .out1(decoder_2_out1), .out2(decoder_2_out2), .out3(decoder_2_out3),
    .out4(decoder_2_out4), .out5(decoder_2_out5), .out6(decoder_2_out6), .out7(decoder_2_out7),
    .sel(IR[14:12]));
  and and_1 (and_1_out, decoder_2_out7, ~IR[15], decoder_1_out4);  // AND_Gate
  and and_2 (and_2_out, decoder_1_out4, IR[15], decoder_2_out7);
  and and_3 (and_3_out, decoder_1_out3, R);
  or or_1 (or_1_out, decoder_2_out0, decoder_2_out1, decoder_2_out2, decoder_2_out5);
  and and_4 (and_4_out, or_1_out, decoder_1_out6);
  and and_5 (and_5_out, decoder_1_out5, decoder_2_out3);
  and and_6 (and_6_out, decoder_2_out4, decoder_1_out5);
  and and_7 (and_7_out, decoder_2_out6, decoder_1_out7);
  or or_2 (T_count_clear, and_1_out, and_3_out, and_4_out, and_5_out, and_6_out, and_7_out, and_2_out);
endmodule

module IR (
  input  Clear,
  input  Load,
  input  Clk,
  input  Increment,
  input  [15:0] Register_IN,
  output [15:0] Register_OUT,
  output HLT
);

  wire and_1_out, and_2_out, and_3_out, and_4_out, and_5_out, and_6_out, and_7_out, and_8_out, and_9_out,
       and_10_out, and_11_out, and_12_out, and_13_out, and_14_out, and_15_out, and_16_out, and_17_out,
       and_18_out, and_19_out, and_20_out, and_21_out, and_22_out, and_23_out, and_24_out, and_25_out,
       and_26_out, and_27_out, and_28_out, and_29_out, and_30_out, and_31_out, and_32_out, and_33_out,
       and_34_out, and_35_out, and_36_out, and_37_out, and_38_out, and_39_out, and_40_out, and_41_out,
       and_42_out, and_43_out, and_44_out, and_45_out, and_46_out, and_47_out, and_48_out, and_49_out,
       not_1_out, not_2_out, not_3_out, not_4_out, not_5_out, not_6_out, not_7_out, not_8_out, not_9_out,
       not_10_out, not_11_out, not_12_out, not_13_out, not_14_out, not_15_out, not_16_out, not_17_out,
       not_18_out, or_1_out, or_2_out, or_3_out, or_4_out, or_5_out, or_6_out, or_7_out, or_8_out, or_9_out,
       or_10_out, or_11_out, or_12_out, or_13_out, or_14_out, or_15_out, or_16_out, or_17_out, or_18_out,
       or_19_out, or_20_out, or_21_out, or_22_out, or_23_out, or_24_out, or_25_out, or_26_out, or_27_out,
       or_28_out, or_29_out, or_30_out, or_31_out, or_32_out;

  not not_1 (not_1_out, Clear);
  not not_2 (not_2_out, Load);
  and and_1 (and_1_out, not_1_out, Load);
  and and_2 (and_2_out, not_1_out, not_2_out, Increment);
  not not_3 (not_3_out, Register_IN[0]);
  not not_4 (not_4_out, Register_IN[1]);
  not not_5 (not_5_out, Register_IN[2]);
  not not_6 (not_6_out, Register_IN[3]);
  not not_7 (not_7_out, Register_IN[4]);
  not not_8 (not_8_out, Register_IN[5]);
  not not_9 (not_9_out, Register_IN[6]);
  not not_10 (not_10_out, Register_IN[7]);
  not not_11 (not_11_out, Register_IN[8]);
  not not_12 (not_12_out, Register_IN[9]);
  not not_13 (not_13_out, Register_IN[10]);
  not not_14 (not_14_out, Register_IN[11]);
  not not_15 (not_15_out, Register_IN[12]);
  not not_16 (not_16_out, Register_IN[13]);
  not not_17 (not_17_out, Register_IN[14]);
  not not_18 (not_18_out, Register_IN[15]);
  and and_3 (and_3_out, and_1_out, Register_IN[0]);
  and and_4 (and_4_out, and_1_out, not_3_out);
  and and_5 (and_5_out, and_2_out, Register_OUT[0]);
  and and_6 (and_6_out, and_1_out, Register_IN[1]);
  and and_7 (and_7_out, and_1_out, not_4_out);
  and and_8 (and_8_out, and_5_out, Register_OUT[1]);
  and and_9 (and_9_out, and_1_out, Register_IN[2]);
  and and_10 (and_10_out, and_1_out, not_5_out);
  and and_11 (and_11_out, and_8_out, Register_OUT[2]);
  and and_12 (and_12_out, and_1_out, Register_IN[3]);
  and and_13 (and_13_out, and_1_out, not_6_out);
  and and_14 (and_14_out, and_1_out, Register_IN[4]);
  and and_15 (and_15_out, and_1_out, not_7_out);
  and and_16 (and_16_out, and_1_out, Register_IN[5]);
  and and_17 (and_17_out, and_1_out, not_8_out);
  and and_18 (and_18_out, and_1_out, Register_IN[6]);
  and and_19 (and_19_out, and_1_out, not_9_out);
  and and_20 (and_20_out, and_1_out, Register_IN[7]);
  and and_21 (and_21_out, and_1_out, not_10_out);
  and and_22 (and_22_out, and_1_out, Register_IN[8]);
  and and_23 (and_23_out, and_1_out, not_11_out);
  and and_24 (and_24_out, and_1_out, Register_IN[9]);
  and and_25 (and_25_out, and_1_out, not_12_out);
  and and_26 (and_26_out, and_1_out, Register_IN[10]);
  and and_27 (and_27_out, and_1_out, not_13_out);
  and and_28 (and_28_out, and_1_out, Register_IN[11]);
  and and_29 (and_29_out, and_1_out, not_14_out);
  and and_30 (and_30_out, and_1_out, Register_IN[12]);
  and and_31 (and_31_out, and_1_out, not_15_out);
  and and_32 (and_32_out, and_1_out, Register_IN[13]);
  and and_33 (and_33_out, and_1_out, not_16_out);
  and and_34 (and_34_out, and_1_out, Register_IN[14]);
  and and_35 (and_35_out, and_1_out, not_17_out);
  and and_36 (and_36_out, and_1_out, Register_IN[15]);
  and and_37 (and_37_out, and_1_out, not_18_out);
  or or_1 (or_1_out, and_2_out, and_3_out);
  or or_2 (or_2_out, Clear, and_2_out, and_4_out);
  or or_3 (or_3_out, and_5_out, and_6_out);
  or or_4 (or_4_out, Clear, and_5_out, and_7_out);
  or or_5 (or_5_out, and_8_out, and_9_out);
  or or_6 (or_6_out, Clear, and_8_out, and_10_out);
  or or_7 (or_7_out, and_11_out, and_12_out);
  or or_8 (or_8_out, Clear, and_11_out, and_13_out);
  and and_38 (and_38_out, and_11_out, Register_OUT[3]);
  or or_9 (or_9_out, and_38_out, and_14_out);
  or or_10 (or_10_out, Clear, and_38_out, and_15_out);
  and and_39 (and_39_out, and_38_out, Register_OUT[4]);
  or or_11 (or_11_out, and_39_out, and_16_out);
  or or_12 (or_12_out, Clear, and_39_out, and_17_out);
  and and_40 (and_40_out, and_39_out, Register_OUT[5]);
  or or_13 (or_13_out, and_40_out, and_18_out);
  or or_14 (or_14_out, Clear, and_40_out, and_19_out);
  and and_41 (and_41_out, and_40_out, Register_OUT[6]);
  or or_15 (or_15_out, and_41_out, and_20_out);
  or or_16 (or_16_out, Clear, and_41_out, and_21_out);
  and and_42 (and_42_out, and_41_out, Register_OUT[7]);
  or or_17 (or_17_out, and_42_out, and_22_out);
  or or_18 (or_18_out, Clear, and_42_out, and_23_out);
  and and_43 (and_43_out, and_42_out, Register_OUT[8]);
  or or_19 (or_19_out, and_43_out, and_24_out);
  or or_20 (or_20_out, Clear, and_43_out, and_25_out);
  and and_44 (and_44_out, and_43_out, Register_OUT[9]);
  or or_21 (or_21_out, and_44_out, and_26_out);
  or or_22 (or_22_out, Clear, and_44_out, and_27_out);
  and and_45 (and_45_out, and_44_out, Register_OUT[10]);
  or or_23 (or_23_out, and_45_out, and_28_out);
  or or_24 (or_24_out, Clear, and_45_out, and_29_out);
  and and_46 (and_46_out, and_45_out, Register_OUT[11]);
  or or_25 (or_25_out, and_46_out, and_30_out);
  or or_26 (or_26_out, Clear, and_46_out, and_31_out);
  and and_47 (and_47_out, and_46_out, Register_OUT[12]);
  or or_27 (or_27_out, and_47_out, and_32_out);
  or or_28 (or_28_out, Clear, and_47_out, and_33_out);
  and and_48 (and_48_out, and_47_out, Register_OUT[13]);
  or or_29 (or_29_out, and_48_out, and_34_out);
  or or_30 (or_30_out, Clear, and_48_out, and_35_out);
  and and_49 (and_49_out, and_48_out, Register_OUT[14]);
  or or_31 (or_31_out, and_49_out, and_36_out);
  or or_32 (or_32_out, Clear, and_49_out, and_37_out);
  J_K_Flip_Flop j_k_ff_1 (.J(or_1_out), .clk(Clk), .K(or_2_out), .Q(Register_OUT[0]));  // open: Qn, preset, en, reset
  J_K_Flip_Flop j_k_ff_2 (.J(or_3_out), .clk(Clk), .K(or_4_out), .Q(Register_OUT[1]));  // open: Qn, preset, en, reset
  J_K_Flip_Flop j_k_ff_3 (.J(or_5_out), .clk(Clk), .K(or_6_out), .Q(Register_OUT[2]));  // open: Qn, preset, en, reset
  J_K_Flip_Flop j_k_ff_4 (.J(or_7_out), .clk(Clk), .K(or_8_out), .Q(Register_OUT[3]));  // open: Qn, preset, en, reset
  J_K_Flip_Flop j_k_ff_5 (.J(or_9_out), .clk(Clk), .K(or_10_out), .Q(Register_OUT[4]));  // open: Qn, preset, en, reset
  J_K_Flip_Flop j_k_ff_6 (.J(or_11_out), .clk(Clk), .K(or_12_out), .Q(Register_OUT[5]));  // open: Qn, preset, en, reset
  J_K_Flip_Flop j_k_ff_7 (.J(or_13_out), .clk(Clk), .K(or_14_out), .Q(Register_OUT[6]));  // open: Qn, preset, en, reset
  J_K_Flip_Flop j_k_ff_8 (.J(or_15_out), .clk(Clk), .K(or_16_out), .Q(Register_OUT[7]));  // open: Qn, preset, en, reset
  J_K_Flip_Flop j_k_ff_9 (.J(or_17_out), .clk(Clk), .K(or_18_out), .Q(Register_OUT[8]));  // open: Qn, preset, en, reset
  J_K_Flip_Flop j_k_ff_10 (
    .J(or_19_out), .clk(Clk), .K(or_20_out), .Q(Register_OUT[9]));  // open: Qn, preset, en, reset
  J_K_Flip_Flop j_k_ff_11 (
    .J(or_21_out), .clk(Clk), .K(or_22_out), .Q(Register_OUT[10]));  // open: Qn, preset, en, reset
  J_K_Flip_Flop j_k_ff_12 (
    .J(or_23_out), .clk(Clk), .K(or_24_out), .Q(Register_OUT[11]));  // open: Qn, preset, en, reset
  J_K_Flip_Flop j_k_ff_13 (
    .J(or_25_out), .clk(Clk), .K(or_26_out), .Q(Register_OUT[12]));  // open: Qn, preset, en, reset
  J_K_Flip_Flop j_k_ff_14 (
    .J(or_27_out), .clk(Clk), .K(or_28_out), .Q(Register_OUT[13]));  // open: Qn, preset, en, reset
  J_K_Flip_Flop j_k_ff_15 (
    .J(or_29_out), .clk(Clk), .K(or_30_out), .Q(Register_OUT[14]));  // open: Qn, preset, en, reset
  J_K_Flip_Flop j_k_ff_16 (
    .J(or_31_out), .clk(Clk), .K(or_32_out), .Q(Register_OUT[15]));  // open: Qn, preset, en, reset
  // AND_Gate and_50 has open pins: in0=Register_OUT[15], in1=and_49_out, out=open
  and and_51 (HLT, Register_OUT[0], ~Register_OUT[1], ~Register_OUT[2], ~Register_OUT[3], ~Register_OUT[4], ~Register_OUT[5], ~Register_OUT[6], ~Register_OUT[7], ~Register_OUT[8], ~Register_OUT[9], ~Register_OUT[10], ~Register_OUT[11], Register_OUT[12], Register_OUT[13], Register_OUT[14], ~Register_OUT[15]);  // AND_Gate

  // Other names for the same wires on the sheet: r0 = Register_IN[0]; r1 = Register_IN[1]; r2 = Register_IN[2];
  //   r3 = Register_IN[3]; r4 = Register_IN[4]; r5 = Register_IN[5]; r6 = Register_IN[6]; r7 = Register_IN[7];
  //   r8 = Register_IN[8]; r9 = Register_IN[9]; r10 = Register_IN[10]; r11 = Register_IN[11]; r12 = Register_IN[12];
  //   r13 = Register_IN[13]; r14 = Register_IN[14]; r15 = Register_IN[15]; d0 = Register_OUT[0]; d1 = Register_OUT[1];
  //   d2 = Register_OUT[2]; d3 = Register_OUT[3]; d4 = Register_OUT[4]; d5 = Register_OUT[5]; d6 = Register_OUT[6];
  //   d7 = Register_OUT[7]; d8 = Register_OUT[8]; d9 = Register_OUT[9]; d10 = Register_OUT[10];
  //   d11 = Register_OUT[11]; d12 = Register_OUT[12]; d13 = Register_OUT[13]; d14 = Register_OUT[14];
  //   d15 = Register_OUT[15]
endmodule

module \RAM_Kontrolü  (
  input  [15:0] IR,
  input  [2:0] T,
  input  R,
  output Load
);

  wire and_1_out, and_2_out, and_3_out, and_4_out, decoder_1_out0, decoder_1_out1, decoder_1_out2,
       decoder_1_out3, decoder_1_out4, decoder_1_out5, decoder_1_out6, decoder_1_out7, decoder_2_out0,
       decoder_2_out1, decoder_2_out2, decoder_2_out3, decoder_2_out4, decoder_2_out5, decoder_2_out6,
       decoder_2_out7, or_1_out;

  Decoder #(.select(3), .enable("false")) decoder_1 (
    .out0(decoder_1_out0), .out1(decoder_1_out1), .out2(decoder_1_out2), .out3(decoder_1_out3),
    .out4(decoder_1_out4), .out5(decoder_1_out5), .out6(decoder_1_out6), .out7(decoder_1_out7), .sel(T));
  Decoder #(.select(3), .enable("false")) decoder_2 (
    .out0(decoder_2_out0), .out1(decoder_2_out1), .out2(decoder_2_out2), .out3(decoder_2_out3),
    .out4(decoder_2_out4), .out5(decoder_2_out5), .out6(decoder_2_out6), .out7(decoder_2_out7),
    .sel(IR[14:12]));
  and and_1 (and_1_out, R, decoder_1_out1);
  and and_2 (and_2_out, decoder_2_out3, decoder_1_out4);
  and and_3 (and_3_out, decoder_2_out5, decoder_1_out4);
  and and_4 (and_4_out, decoder_2_out6, decoder_1_out6);
  or or_1 (or_1_out, and_1_out, and_2_out, and_3_out, and_4_out);
  not not_1 (Load, or_1_out);
endmodule

module \IR_Kontrolü  (
  input  [2:0] T,
  input  R,
  output Load
);

  wire decoder_1_out1;

  Decoder #(.select(3), .enable("false")) decoder_1 (
    .out1(decoder_1_out1), .sel(T));  // open: out0, out2, out3, out4, out5, out6, out7
  and and_1 (Load, ~R, decoder_1_out1);  // AND_Gate
endmodule

module \AR_Kontrolü  (
  input  [15:0] IR,
  input  [2:0] T,
  input  R,
  output Load,
  output Clear,
  output Increment
);

  wire and_1_out, and_2_out, and_3_out, decoder_1_out0, decoder_1_out1, decoder_1_out2, decoder_1_out3,
       decoder_1_out4, decoder_1_out5, decoder_1_out6, decoder_1_out7, decoder_2_out0, decoder_2_out1,
       decoder_2_out2, decoder_2_out3, decoder_2_out4, decoder_2_out5, decoder_2_out6, decoder_2_out7;

  Decoder #(.select(3), .enable("false")) decoder_1 (
    .out0(decoder_1_out0), .out1(decoder_1_out1), .out2(decoder_1_out2), .out3(decoder_1_out3),
    .out4(decoder_1_out4), .out5(decoder_1_out5), .out6(decoder_1_out6), .out7(decoder_1_out7), .sel(T));
  Decoder #(.select(3), .enable("false")) decoder_2 (
    .out0(decoder_2_out0), .out1(decoder_2_out1), .out2(decoder_2_out2), .out3(decoder_2_out3),
    .out4(decoder_2_out4), .out5(decoder_2_out5), .out6(decoder_2_out6), .out7(decoder_2_out7),
    .sel(IR[14:12]));
  and and_1 (and_1_out, ~R, decoder_1_out0);  // AND_Gate
  and and_2 (and_2_out, ~decoder_2_out7, IR[15], decoder_1_out3);  // AND_Gate
  and and_3 (and_3_out, ~R, decoder_1_out2);  // AND_Gate
  and and_4 (Clear, R, decoder_1_out0);
  and and_5 (Increment, decoder_2_out5, decoder_1_out4);
  or or_1 (Load, and_1_out, and_2_out, and_3_out);
endmodule

module \PC_Kontrolü  (
  input  R,
  input  [15:0] IR,
  input  [15:0] DR,
  input  [15:0] AC,
  input  [2:0] T,
  input  FGI,
  input  FGO,
  input  E,
  output Load,
  output Increment,
  output Clear
);

  wire and_3_out, and_4_out, and_5_out, and_6_out, and_7_out, and_8_out, and_9_out, and_10_out, and_11_out,
       and_12_out, and_13_out, decoder_1_out0, decoder_1_out1, decoder_1_out2, decoder_1_out3,
       decoder_1_out4, decoder_1_out5, decoder_1_out6, decoder_1_out7, decoder_2_out0, decoder_2_out1,
       decoder_2_out2, decoder_2_out3, decoder_2_out4, decoder_2_out5, decoder_2_out6, decoder_2_out7,
       not_1_out, not_2_out, or_2_out, or_4_out, p, r_t;

  Decoder #(.select(3), .enable("false")) decoder_1 (
    .out0(decoder_1_out0), .out1(decoder_1_out1), .out2(decoder_1_out2), .out3(decoder_1_out3),
    .out4(decoder_1_out4), .out5(decoder_1_out5), .out6(decoder_1_out6), .out7(decoder_1_out7), .sel(T));
  Decoder #(.select(3), .enable("false")) decoder_2 (
    .out0(decoder_2_out0), .out1(decoder_2_out1), .out2(decoder_2_out2), .out3(decoder_2_out3),
    .out4(decoder_2_out4), .out5(decoder_2_out5), .out6(decoder_2_out6), .out7(decoder_2_out7),
    .sel(IR[14:12]));
  and and_1 (p, decoder_2_out7, IR[15], decoder_1_out3);
  and and_2 (r_t, decoder_2_out7, ~IR[15], decoder_1_out3);  // AND_Gate
  not not_1 (not_1_out, or_2_out);
  and and_3 (and_3_out, decoder_2_out4, decoder_1_out4);
  or or_1 (Load, and_3_out, and_4_out);
  and and_4 (and_4_out, decoder_2_out5, decoder_1_out5);
  and and_5 (and_5_out, ~R, decoder_1_out1);  // AND_Gate
  and and_6 (and_6_out, R, decoder_1_out2);
  and and_7 (and_7_out, decoder_1_out6, decoder_2_out6, not_1_out);
  and and_8 (and_8_out, ~AC[15], IR[4], r_t);  // AND_Gate
  and and_9 (and_9_out, AC[15], IR[3], r_t);
  and and_10 (and_10_out, not_2_out, IR[2], r_t);
  and and_11 (and_11_out, ~E, IR[1], r_t);  // AND_Gate
  and and_12 (and_12_out, IR[9], FGI, p);
  and and_13 (and_13_out, IR[8], FGO, p);
  and and_14 (Clear, R, decoder_1_out1);
  or or_2 (or_2_out, DR[15], DR[14], DR[13], DR[12], DR[11], DR[10], DR[9], DR[8], DR[7], DR[6], DR[5], DR[4], DR[3], DR[2], DR[1], DR[0]);
  not not_2 (not_2_out, or_4_out);
  or or_3 (Increment, and_5_out, and_6_out, and_7_out, and_8_out, and_9_out, and_10_out, and_11_out, and_12_out, and_13_out);
  or or_4 (or_4_out, AC[15], AC[14], AC[13], AC[12], AC[11], AC[10], AC[9], AC[8], AC[7], AC[6], AC[5], AC[4], AC[3], AC[2], AC[1], AC[0]);
endmodule

module E (
  input  E_IN,
  input  Comp,
  input  load,
  input  Clock,
  input  Clear,
  output E_OUT
);

  wire and_1_out, multiplexer_1_out;

  Multiplexer #(.enable("false")) multiplexer_1 (.in0(E_IN), .in1(Comp), .out(multiplexer_1_out), .sel(Comp));
  and and_1 (and_1_out, multiplexer_1_out, Comp);
  J_K_Flip_Flop j_k_ff_1 (
    .J(multiplexer_1_out), .clk(Clock), .K(and_1_out), .Q(E_OUT), .en(load), .reset(Clear));  // open: Qn, preset
endmodule

module \E_Kontrolü  (
  input  [15:0] IR,
  input  [2:0] T,
  output Comp,
  output Clear,
  output Load
);

  wire and_5_out, and_6_out, and_7_out, decoder_1_out0, decoder_1_out1, decoder_1_out2, decoder_1_out3,
       decoder_1_out4, decoder_1_out5, decoder_1_out6, decoder_1_out7, decoder_2_out0, decoder_2_out1,
       decoder_2_out2, decoder_2_out3, decoder_2_out4, decoder_2_out5, decoder_2_out6, decoder_2_out7, p, r;

  Decoder #(.select(3), .enable("false")) decoder_1 (
    .out0(decoder_1_out0), .out1(decoder_1_out1), .out2(decoder_1_out2), .out3(decoder_1_out3),
    .out4(decoder_1_out4), .out5(decoder_1_out5), .out6(decoder_1_out6), .out7(decoder_1_out7), .sel(T));
  Decoder #(.select(3), .enable("false")) decoder_2 (
    .out0(decoder_2_out0), .out1(decoder_2_out1), .out2(decoder_2_out2), .out3(decoder_2_out3),
    .out4(decoder_2_out4), .out5(decoder_2_out5), .out6(decoder_2_out6), .out7(decoder_2_out7),
    .sel(IR[14:12]));
  and and_1 (p, decoder_1_out3, IR[15], decoder_2_out7);
  and and_2 (r, decoder_1_out3, ~IR[15], decoder_2_out7);  // AND_Gate
  and and_3 (Comp, IR[8], r);
  and and_4 (Clear, IR[10], r);
  and and_5 (and_5_out, decoder_2_out1, decoder_1_out5);
  and and_6 (and_6_out, IR[7], r);
  and and_7 (and_7_out, IR[6], r);
  or or_1 (Load, and_5_out, and_6_out, and_7_out);
endmodule

module \DR_Kontrolü  (
  input  [15:0] IR,
  input  [2:0] T,
  output Load,
  output Increment
);

  wire decoder_1_out0, decoder_1_out1, decoder_1_out2, decoder_1_out3, decoder_1_out4, decoder_1_out5,
       decoder_1_out6, decoder_1_out7, decoder_2_out0, decoder_2_out1, decoder_2_out2, decoder_2_out3,
       decoder_2_out4, decoder_2_out5, decoder_2_out6, decoder_2_out7, or_1_out;

  Decoder #(.select(3), .enable("false")) decoder_1 (
    .out0(decoder_1_out0), .out1(decoder_1_out1), .out2(decoder_1_out2), .out3(decoder_1_out3),
    .out4(decoder_1_out4), .out5(decoder_1_out5), .out6(decoder_1_out6), .out7(decoder_1_out7), .sel(T));
  Decoder #(.select(3), .enable("false")) decoder_2 (
    .out0(decoder_2_out0), .out1(decoder_2_out1), .out2(decoder_2_out2), .out3(decoder_2_out3),
    .out4(decoder_2_out4), .out5(decoder_2_out5), .out6(decoder_2_out6), .out7(decoder_2_out7),
    .sel(IR[14:12]));
  and and_1 (Increment, decoder_2_out6, decoder_1_out5);
  or or_1 (or_1_out, decoder_2_out0, decoder_2_out1, decoder_2_out2, decoder_2_out6);
  and and_2 (Load, decoder_1_out4, or_1_out);
endmodule

module \AC_Kontrolü  (
  input  [15:0] IR,
  input  [2:0] T,
  output Clear,
  output Increment,
  output LOAD
);

  wire and_5_out, and_6_out, and_7_out, and_8_out, and_9_out, and_10_out, and_11_out, decoder_1_out0,
       decoder_1_out1, decoder_1_out2, decoder_1_out3, decoder_1_out4, decoder_1_out5, decoder_1_out6,
       decoder_1_out7, decoder_2_out0, decoder_2_out1, decoder_2_out2, decoder_2_out3, decoder_2_out4,
       decoder_2_out5, decoder_2_out6, decoder_2_out7, p, r;

  Decoder #(.select(3), .enable("false")) decoder_1 (
    .out0(decoder_1_out0), .out1(decoder_1_out1), .out2(decoder_1_out2), .out3(decoder_1_out3),
    .out4(decoder_1_out4), .out5(decoder_1_out5), .out6(decoder_1_out6), .out7(decoder_1_out7), .sel(T));
  Decoder #(.select(3), .enable("false")) decoder_2 (
    .out0(decoder_2_out0), .out1(decoder_2_out1), .out2(decoder_2_out2), .out3(decoder_2_out3),
    .out4(decoder_2_out4), .out5(decoder_2_out5), .out6(decoder_2_out6), .out7(decoder_2_out7),
    .sel(IR[14:12]));
  and and_1 (p, decoder_1_out3, IR[15], decoder_2_out7);
  and and_2 (r, decoder_1_out3, ~IR[15], decoder_2_out7);  // AND_Gate
  and and_3 (Clear, IR[11], r);
  and and_4 (Increment, IR[5], r);
  and and_5 (and_5_out, decoder_2_out0, decoder_1_out5);
  and and_6 (and_6_out, decoder_2_out1, decoder_1_out5);
  and and_7 (and_7_out, decoder_2_out2, decoder_1_out5);
  and and_8 (and_8_out, IR[7], r);
  and and_9 (and_9_out, IR[6], r);
  and and_10 (and_10_out, IR[11], p);
  and and_11 (and_11_out, IR[9], r);
  or or_1 (LOAD, and_5_out, and_6_out, and_7_out, and_9_out, and_8_out, and_11_out, and_10_out);
endmodule

module \TR_Kontrolü  (
  input  [2:0] T,
  input  R,
  output Load
);

  wire decoder_1_out0, decoder_1_out1, decoder_1_out2, decoder_1_out3, decoder_1_out4, decoder_1_out5,
       decoder_1_out6, decoder_1_out7;

  Decoder #(.select(3), .enable("false")) decoder_1 (
    .out0(decoder_1_out0), .out1(decoder_1_out1), .out2(decoder_1_out2), .out3(decoder_1_out3),
    .out4(decoder_1_out4), .out5(decoder_1_out5), .out6(decoder_1_out6), .out7(decoder_1_out7), .sel(T));
  and and_1 (Load, R, decoder_1_out0);
endmodule

module \OUTR_Kontrolü  (
  input  [15:0] IR,
  input  [2:0] T,
  output LD,
  output Clear
);

  wire and_3_out, decoder_1_out0, decoder_1_out1, decoder_1_out3, decoder_2_out7, or_1_out, p;

  Decoder #(.select(3), .enable("false")) decoder_1 (
    .out0(decoder_1_out0), .out1(decoder_1_out1), .out3(decoder_1_out3), .sel(T));  // open: out2, out4, out5, out6, out7
  Decoder #(.select(3), .enable("false")) decoder_2 (
    .out7(decoder_2_out7), .sel(IR[14:12]));  // open: out0, out1, out2, out3, out4, out5, out6
  and and_1 (p, decoder_1_out3, IR[15], decoder_2_out7);
  and and_2 (LD, IR[10], p);
  and and_3 (and_3_out, IR[11], p);
  or or_1 (or_1_out, decoder_1_out0, decoder_1_out1);
  or or_2 (Clear, and_3_out, or_1_out);
endmodule

module \İnput_Kontrol  (
  input  [2:0] T,
  output LOAD
);

  wire decoder_1_out0;

  Decoder #(.select(3), .enable("false")) decoder_1 (
    .out0(decoder_1_out0), .sel(T));  // open: out1, out2, out3, out4, out5, out6, out7
  and and_1 (LOAD, decoder_1_out0, 1'b1);
endmodule

module OUT_Kontrol (
  input  [15:0] IR,
  input  [2:0] T,
  output LD
);

  wire decoder_1_out0, decoder_2_out7, p;

  Decoder #(.select(3), .enable("false")) decoder_1 (
    .out0(decoder_1_out0), .sel(T));  // open: out1, out2, out3, out4, out5, out6, out7
  Decoder #(.select(3), .enable("false")) decoder_2 (
    .out7(decoder_2_out7), .sel(IR[14:12]));  // open: out0, out1, out2, out3, out4, out5, out6
  and and_1 (p, decoder_1_out0, IR[15], decoder_2_out7);
  and and_2 (LD, IR[10], p);
endmodule

module INP_Kontrol (
  input  [15:0] IR,
  input  [2:0] T,
  output LD
);

  wire decoder_1_out0, decoder_2_out7, p;

  Decoder #(.select(3), .enable("false")) decoder_1 (
    .out0(decoder_1_out0), .sel(T));  // open: out1, out2, out3, out4, out5, out6, out7
  Decoder #(.select(3), .enable("false")) decoder_2 (
    .out7(decoder_2_out7), .sel(IR[14:12]));  // open: out0, out1, out2, out3, out4, out5, out6
  and and_1 (p, decoder_1_out0, IR[15], decoder_2_out7);
  and and_2 (LD, IR[11], p);
endmodule
